// Logisim project different_types_of_gates.circ as structural Verilog: 1 circuit, main circuit main
// NOT
module main (
  input  in1,
  input  in_1,
  input  in2,
  input  in1_2,
  input  in2_2,
  input  in1_3,
  input  in1_4,
  input  in2_3,
  input  in2_4,
  input  in1_5,
  input  in2_5,
  output out,
  output out_2,
  output out_3,
  output out_4,
  output out_5,
  output out_6
);

  not not_1 (out, in_1);
  and and_1 (out_3, in1_2, in2_2);
  or or_1 (out_5, in1_4, in2_4);
  xor xor_1 (out_6, in1_5, in2_5);
  nand nand_1 (out_2, in1, in2);
  nor nor_1 (out_4, in1_3, in2_3);

  // Notes on the sheet:
  //   NOT GATE
  //   AND GATE
  //   OR GATE
  //   XOR GATE
  //    VERIFYING THE LOGIC GATES
  //   NAND GATE
  //   NOR GATE
endmodule
