// Logisim project BASIC_GATES_USING_NAND.circ as structural Verilog: 1 circuit, main circuit main
module main (
  input  in_1,
  input  in_2,
  input  in_3,
  input  in_4,
  input  in_5,
  input  in_6,
  input  in_7,
  input  AND_GATE,
  input  in_9,
  input  in_10,
  input  in_11,
  input  in_12,
  input  in_13,
  input  in_14,
  input  in_15,
  input  in_16,
  input  in_17,
  input  in_18,
  output out_19,
  output out_20,
  output out_21,
  output out_22,
  output out_23,
  output out_24,
  output out_25,
  output out_26,
  output out_27,
  output out_28
);

  wire n7400_1_pin3, n7400_2_pin1, n7400_2_pin2, n7400_3_pin1, n7400_3_pin2, n7400_3_pin3, n7400_4_pin3,
       n7400_5_pin3, n7400_6_pin11, nand_1_out, nand_2_out, nand_4_out, nand_5_out, nand_6_out, nand_7_out,
       nand_9_out, nand_10_out, nand_11_out;

  _7400 not_gate (
    .pin1(in_10), .pin2(in_10), .pin3(out_24));  // open: pin4, pin5, pin6, pin13, pin12, pin11, pin10, pin9, pin8
  _7400 u_7400_1 (
    .pin1(in_11), .pin2(in_12), .pin3(n7400_1_pin3));  // open: pin4, pin5, pin6, pin13, pin12, pin11, pin10, pin9, pin8
  _7400 u_7400_2 (
    .pin1(n7400_2_pin1), .pin2(n7400_2_pin2), .pin3(out_26));  // open: pin4, pin5, pin6, pin13, pin12, pin11, pin10, pin9, pin8
  not not_1 (n7400_2_pin1, in_13);
  not not_2 (n7400_2_pin2, in_14);
  _7400 u_7400_3 (
    .pin1(n7400_3_pin1), .pin2(n7400_3_pin2), .pin3(n7400_3_pin3));  // open: pin4, pin5, pin6, pin13, pin12, pin11, pin10, pin9, pin8
  not not_3 (n7400_3_pin1, in_15);
  not not_4 (n7400_3_pin2, in_16);
  _7400 u_7400_4 (
    .pin1(in_17), .pin2(in_18), .pin3(n7400_4_pin3));  // open: pin4, pin5, pin6, pin13, pin12, pin11, pin10, pin9, pin8
  nand nand_1 (nand_1_out, in_6, in_7);
  nand nand_2 (nand_2_out, AND_GATE, in_9);
  not not_5 (out_25, n7400_1_pin3);
  not not_6 (out_27, n7400_3_pin3);
  nand nand_3 (out_19, in_1, in_1);
  nand nand_4 (nand_4_out, in_2, in_2);
  nand nand_5 (nand_5_out, in_3, in_3);
  nand nand_6 (nand_6_out, in_4, in_4);
  nand nand_7 (nand_7_out, in_5, in_5);
  _7400 u_7400_5 (
    .pin1(in_17), .pin2(n7400_4_pin3), .pin3(n7400_5_pin3));  // open: pin4, pin5, pin6, pin13, pin12, pin11, pin10, pin9, pin8
  _7400 u_7400_6 (
    .pin13(in_18), .pin12(n7400_4_pin3), .pin11(n7400_6_pin11));  // open: pin1, pin2, pin3, pin4, pin5, pin6, pin10, pin9, pin8
  nand nand_8 (out_20, nand_4_out, nand_5_out);
  nand nand_9 (nand_9_out, nand_6_out, nand_7_out);
  nand nand_10 (nand_10_out, in_6, nand_1_out);
  nand nand_11 (nand_11_out, nand_1_out, in_7);
  nand nand_12 (out_23, nand_2_out, nand_2_out);
  not not_7 (out_21, nand_9_out);
  _7400 u_7400_7 (
    .pin1(n7400_6_pin11), .pin2(n7400_5_pin3), .pin3(out_28));  // open: pin4, pin5, pin6, pin13, pin12, pin11, pin10, pin9, pin8
  nand nand_13 (out_22, nand_10_out, nand_11_out);

  // Notes on the sheet:
  //   NOT GATE
  //   OR GATE
  //    NOR GATE
  //   XOR GATE
  //   NOT GATE
  //   AND GATE
  //   OR GATE
  //   NOR GATE
  //   XOR GATE
  //   BASIC LOGIC GATES USING NAND GATE
  //   BASIC GATES  USING NAND GATES USING IC
endmodule
