// Logisim project practice_problems.circ as structural Verilog: 1 circuit, main circuit main
module main (
  input  B,
  input  C,
  input  A,
  input  in_4,
  input  in_5,
  input  in_6,
  input  in_7,
  input  in_8,
  input  in_9,
  input  in_10,
  input  in_11,
  input  in_12,
  input  in_13,
  input  in_14,
  input  in_15,
  input  in_16,
  input  in_17,
  input  in_18,
  input  in_19,
  input  in_20,
  input  in_21,
  input  in_22,
  output out_23,
  output out_24,
  output out_25,
  output out_26,
  output out_27
);

  wire and_1_out, and_2_out, and_3_out, and_4_out, and_5_out, and_6_out, and_7_out, and_8_out, nand_1_out,
       nand_2_out, nand_3_out, nand_4_out, not_1_out, not_2_out, not_3_out, not_4_out, not_5_out, not_6_out,
       not_7_out, not_8_out, not_9_out, not_10_out, not_11_out, not_12_out, not_13_out, not_14_out,
       not_15_out, not_16_out, not_17_out, or_2_out, or_3_out, or_4_out, or_5_out, or_6_out, or_7_out,
       or_8_out, or_9_out;

  not not_1 (not_1_out, in_10);
  not not_2 (not_2_out, C);
  not not_3 (not_3_out, B);
  not not_4 (not_4_out, in_9);
  not not_5 (not_5_out, in_13);
  not not_6 (not_6_out, in_18);
  not not_7 (not_7_out, in_5);
  not not_8 (not_8_out, in_4);
  not not_9 (not_9_out, in_6);
  and and_1 (and_1_out, in_8, not_4_out);
  and and_2 (and_2_out, in_9, not_1_out);
  and and_3 (and_3_out, in_7, in_6, in_5, in_4);
  nand nand_1 (nand_1_out, B, C);
  nand nand_2 (nand_2_out, not_3_out, not_2_out, A);
  nand nand_3 (nand_3_out, B, not_3_out, A);
  and and_4 (and_4_out, not_7_out, not_8_out);
  // OR_Gate or_1 has open pins: in0=and_1_out, in1=and_2_out, out=open
  and and_5 (and_5_out, not_9_out, in_5, in_4);
  and and_6 (and_6_out, in_4, not_9_out);
  and and_7 (and_7_out, in_11, in_12);
  or or_2 (or_2_out, not_5_out, in_16, in_14);
  or or_3 (or_3_out, in_17, not_5_out, in_14);
  or or_4 (or_4_out, in_15, in_16, not_5_out);
  or or_5 (or_5_out, not_5_out, in_15, in_17);
  or or_6 (or_6_out, not_6_out, in_21, in_19);
  or or_7 (or_7_out, in_22, not_6_out, in_19);
  or or_8 (or_8_out, in_20, in_21, not_6_out);
  or or_9 (or_9_out, not_6_out, in_20, in_22);
  and and_8 (and_8_out, not_7_out, in_4);
  nand nand_4 (nand_4_out, in_8, and_1_out);
  not not_10 (not_10_out, or_6_out);
  not not_11 (not_11_out, or_7_out);
  not not_12 (not_12_out, or_8_out);
  not not_13 (not_13_out, or_9_out);
  or or_10 (out_25, nand_4_out, and_7_out);
  and and_9 (out_26, or_2_out, or_3_out, or_4_out, or_5_out);
  not not_14 (not_14_out, not_10_out);
  not not_15 (not_15_out, not_11_out);
  not not_16 (not_16_out, not_12_out);
  not not_17 (not_17_out, not_13_out);
  and and_10 (out_23, nand_1_out, nand_2_out, nand_3_out);
  or or_11 (out_24, and_3_out, and_4_out, and_5_out, and_6_out, and_8_out);
  nor nor_1 (out_27, not_14_out, not_15_out, not_16_out, not_17_out);

  // Notes on the sheet:
  //   1.
  //   2.
  //   3.
  //   4.
  //   5.
  //   LOGIC GATE CIRCUITS IN LOGISIM
endmodule
