// Logisim project booleanexpressions_to_logic_gates_and_viceversa.circ as structural Verilog: 1 circuit, main circuit main
module main (
  input  A,
  input  B,
  input  C,
  input  A_2,
  input  B_2,
  input  C_2,
  input  A_3,
  input  B_3,
  input  C_3,
  input  D,
  input  A_4,
  input  B_4,
  input  C_4,
  input  A_5,
  input  B_5,
  input  C_5,
  input  D_2,
  input  A_6,
  input  B_6,
  input  C_6,
  input  A_7,
  input  B_7,
  input  C_7,
  input  A_8,
  input  B_8,
  input  C_8,
  input  D_3,
  input  A_9,
  input  B_9,
  input  C_9,
  input  D_4,
  output out_32,
  output out_33,
  output out_34,
  output out_35,
  output out_36,
  output out_37,
  output out_38,
  output out_39,
  output out_40
);

  wire and_1_out, and_2_out, and_3_out, and_4_out, and_5_out, and_6_out, and_7_out, and_8_out, and_9_out,
       and_10_out, and_11_out, and_12_out, and_13_out, and_14_out, and_15_out, and_16_out, and_17_out,
       and_18_out, and_19_out, and_20_out, and_21_out, and_22_out, and_23_out, and_24_out, and_26_out,
       and_27_out, and_28_out, not_1_out, not_2_out, not_3_out, not_4_out, not_5_out, not_6_out, not_7_out,
       not_8_out, not_9_out, not_10_out, not_11_out, not_12_out, not_13_out, or_1_out, or_2_out, or_3_out,
       or_4_out, or_5_out, or_6_out, or_7_out, or_9_out, or_10_out, or_11_out, or_12_out, or_14_out,
       or_16_out, or_17_out;

  and and_1 (and_1_out, A, B);
  and and_2 (and_2_out, B, C);
  or or_1 (or_1_out, B, C);
  not not_1 (not_1_out, A_3);
  not not_2 (not_2_out, B_3);
  not not_3 (not_3_out, C_3);
  not not_4 (not_4_out, A_4);
  not not_5 (not_5_out, A_4);
  not not_6 (not_6_out, A_5);
  not not_7 (not_7_out, B_5);
  not not_8 (not_8_out, D_2);
  not not_9 (not_9_out, B_8);
  and and_3 (and_3_out, A_2, C_2);
  or or_2 (or_2_out, A_2, C_2);
  and and_4 (and_4_out, not_4_out, B_4);
  and and_5 (and_5_out, A_5, C_5, not_7_out);
  and and_6 (and_6_out, B_5, not_8_out);
  and and_7 (and_7_out, A_5, B_5, not_8_out);
  and and_8 (and_8_out, A_6, B_6);
  or or_3 (or_3_out, B_6, C_6);
  and and_9 (and_9_out, B_6, C_6);
  or or_4 (or_4_out, A_7, B_7);
  and and_10 (and_10_out, B_7, C_7);
  or or_5 (or_5_out, C_7, A_7);
  not not_10 (not_10_out, C_9);
  and and_11 (and_11_out, and_2_out, or_1_out);
  and and_12 (and_12_out, not_2_out, C_3);
  and and_13 (and_13_out, not_3_out, D);
  and and_14 (and_14_out, not_5_out, C_4);
  and and_15 (and_15_out, A_8, B_8);
  or or_6 (or_6_out, not_9_out, C_8);
  and and_16 (and_16_out, C_8, D_3);
  or or_7 (or_7_out, B_9, C_9);
  or or_8 (out_32, and_1_out, and_11_out);
  and and_17 (and_17_out, or_2_out, B_2);
  or or_9 (or_9_out, and_12_out, and_13_out);
  or or_10 (or_10_out, and_4_out, C_4);
  or or_11 (or_11_out, B_4, and_14_out);
  and and_18 (and_18_out, not_6_out, C_5);
  and and_19 (and_19_out, C_5, A_5);
  and and_20 (and_20_out, or_3_out, and_9_out);
  not not_11 (not_11_out, or_6_out);
  and and_21 (and_21_out, A_9, B_9);
  or or_12 (or_12_out, B_9, or_7_out);
  and and_22 (and_22_out, not_10_out, D_4);
  or or_13 (out_33, and_3_out, A_2, and_17_out);
  or or_14 (or_14_out, and_19_out, B_5);
  and and_23 (and_23_out, or_4_out, and_10_out);
  not not_12 (not_12_out, or_5_out);
  and and_24 (and_24_out, B_3, or_9_out);
  and and_25 (out_35, or_10_out, or_11_out);
  and and_26 (and_26_out, and_18_out, or_14_out);
  or or_15 (out_37, and_8_out, and_20_out);
  not not_13 (not_13_out, and_23_out);
  and and_27 (and_27_out, and_15_out, not_11_out);
  or or_16 (or_16_out, not_11_out, and_16_out);
  and and_28 (and_28_out, and_21_out, or_12_out);
  or or_17 (or_17_out, or_12_out, and_22_out);
  or or_18 (out_36, and_26_out, and_5_out, B_5, and_6_out, and_7_out);
  or or_19 (out_34, not_1_out, and_24_out);
  and and_29 (out_38, not_13_out, not_12_out);
  and and_30 (out_39, and_27_out, or_16_out);
  and and_31 (out_40, and_28_out, or_17_out);

  // Notes on the sheet:
  //   1.
  //   2.
  //   3.
  //   4. 
  //   1.AB+BC(B+C)
  //   2.A+B(A+C)+AC
  //   AB
  //   3:~A+B(~C AND D+~ B ANDC)
  //   ~A
  //   4: ((~A AND B)+C) ((~A AND C)+B)
  //   BC
  //   B+C
  //   5: (A AND ~B ANDC)+B+(B AND ~D)+(A AND B AND ~D)+ (~A ANDC) (AC+B)
  //   A AND ~B AND C
  //   B AND ~D
  //   AB
  //   BC
  //   B+C
  //   A+B
  //   BC
  //   A+C
  //   BC(B+C)
  //   AC
  //   A+C
  //   ~B AND C
  //   ~C AND D
  //   ~A AND B
  //   A  AND B AND ~D
  //   AB
  //   CD
  //   BOOLEAN EXPRESSIONS TO LOGIC GATES
  //   B(A+C)
  //   (~A AND B)+C
  //   LOGIC GATES TO BOOLEAN EXPRESSIONS
  //   BC(B+C)
  //   ~(C+~B)
  //   AB
  //   B+(B+C)
  //   (~C AND D)
  //   ~C AND D + ~B AND C
  //   (~A AND C )+B
  //   ~(A+C)
  //   AB+BC(B+C)
  //   B(~C AND D + ~B AND C)
  //   (~A AND C)(AC+B) 
  //   ((AB)~(C+~B))
  //   ((~(C+~B))+CD)
  //   A+B(A+C)+AC
  //   ANS: AB+ BC(B+C)
  //   (~(A+B)(BC))
  //   ((AB)(B+(B+C)))
  //   ((B+(B+C)) +(~C AND D))
  //    (~A AND B+C) (~A AND C+B)
  //   ANS : ((~(A+B)(BC))(~(A+C))) 
  //   ANS:((AB) ~(C+~B)) AND ((~(C+~B))+ CD)
  //   ANS:((AB)(B+(B+C)))  AND ((B+(B+C)) +(~C AND D)) 
  //   ~A+B(~C AND D+~ B ANDC)
  //   A AND ~B ANDC+B+B AND ~D+A AND B AND ~D+ (~A ANDC) (AC+B)
endmodule
