// Logisim project FULL_AND_HALF_ADDERS_AND_SUBTRACTORS.circ as structural Verilog: 1 circuit, main circuit main
module main (
  input  A,
  input  B,
  input  A_2,
  input  B_2,
  input  A_3,
  input  B_3,
  input  C,
  input  A_4,
  input  B_4,
  input  C_2,
  input  A_5,
  input  B_5,
  input  A_6,
  input  B_6,
  input  A_7,
  input  B_7,
  input  C_3,
  input  A_8,
  input  B_8,
  input  C_4
);

  wire and_1_out, and_2_out, and_3_out, and_4_out, and_5_out, and_6_out, and_7_out, and_8_out, and_9_out,
       and_10_out, and_11_out, and_12_out, and_13_out, and_14_out, and_15_out, and_16_out, not_1_out,
       not_2_out, not_3_out, not_4_out, not_5_out, not_6_out, not_7_out, not_8_out, not_9_out, not_10_out,
       not_11_out, not_12_out, not_13_out, not_14_out, not_15_out, not_16_out, not_17_out, not_18_out,
       not_19_out, not_20_out, not_21_out, not_22_out, not_23_out, not_24_out, not_25_out, not_26_out,
       not_27_out, or_1_out, or_2_out, or_3_out, or_4_out, or_5_out, or_6_out, or_7_out, or_8_out, or_9_out,
       or_10_out, or_11_out, or_12_out, or_13_out, or_14_out, or_15_out, or_16_out, or_17_out, or_18_out,
       or_19_out, or_20_out, or_21_out, or_22_out, or_23_out, or_24_out, or_25_out, or_26_out, or_27_out,
       or_28_out, rgbled_4_p2, xor_1_out, xor_2_out, xor_3_out, xor_4_out, xor_5_out, xor_6_out;

  not not_1 (not_1_out, A_2);
  xor xor_1 (xor_1_out, A_2, B_2);
  // RGBLED rgbled_1: pin names not known; wires that end beside it: xor_1_out
  and and_1 (and_1_out, not_1_out, B_2);
  // RGBLED rgbled_2: pin names not known; wires that end beside it: and_1_out
  not not_2 (not_2_out, A_4);
  not not_3 (not_3_out, A_5);
  not not_4 (not_4_out, B_5);
  not not_5 (not_5_out, A_6);
  not not_6 (not_6_out, B_6);
  xor xor_2 (xor_2_out, A, B);
  // RGBLED rgbled_3: pin names not known; wires that end beside it: xor_2_out
  and and_2 (and_2_out, A, B);
  // RGBLED rgbled_4: pin names not known; wires that end beside it: and_2_out, rgbled_4_p2, rgbled_4_p2
  and and_3 (and_3_out, A_3, B_3);
  and and_4 (and_4_out, B_3, C);
  and and_5 (and_5_out, A_3, C);
  and and_6 (and_6_out, not_2_out, B_4);
  and and_7 (and_7_out, not_2_out, C_2);
  and and_8 (and_8_out, B_4, C_2);
  or or_1 (or_1_out, A_5, B_5);
  or or_2 (or_2_out, not_3_out, not_4_out);
  or or_3 (or_3_out, not_4_out, A_5);
  not not_7 (not_7_out, A_5);
  or or_4 (or_4_out, not_7_out, B_5);
  or or_5 (or_5_out, A_5, B_5);
  or or_6 (or_6_out, A_6, B_6);
  or or_7 (or_7_out, A_7, B_7, C_3);
  not not_8 (not_8_out, B_7);
  or or_8 (or_8_out, A_7, not_8_out, not_9_out);
  not not_9 (not_9_out, C_3);
  not not_10 (not_10_out, A_7);
  or or_9 (or_9_out, not_10_out, B_7, not_11_out);
  not not_11 (not_11_out, C_3);
  not not_12 (not_12_out, A_7);
  not not_13 (not_13_out, B_7);
  or or_10 (or_10_out, not_12_out, not_13_out, C_3);
  or or_11 (or_11_out, A_7, B_7, C_3);
  or or_12 (or_12_out, A_7, B_7, not_14_out);
  not not_14 (not_14_out, C_3);
  not not_15 (not_15_out, B_7);
  or or_13 (or_13_out, A_7, not_15_out, C_3);
  not not_16 (not_16_out, A_7);
  or or_14 (or_14_out, not_16_out, B_7, C_3);
  or or_15 (or_15_out, A_8, B_8, C_4);
  not not_17 (not_17_out, B_8);
  or or_16 (or_16_out, A_8, not_17_out, not_18_out);
  not not_18 (not_18_out, C_4);
  not not_19 (not_19_out, A_8);
  or or_17 (or_17_out, not_19_out, B_8, not_20_out);
  not not_20 (not_20_out, C_4);
  not not_21 (not_21_out, A_8);
  not not_22 (not_22_out, B_8);
  or or_18 (or_18_out, not_21_out, not_22_out, C_4);
  or or_19 (or_19_out, A_8, B_8, C_4);
  not not_23 (not_23_out, A_8);
  or or_20 (or_20_out, not_23_out, B_8, C_4);
  not not_24 (not_24_out, A_8);
  or or_21 (or_21_out, not_24_out, B_8, not_25_out);
  not not_25 (not_25_out, C_4);
  not not_26 (not_26_out, A_8);
  not not_27 (not_27_out, B_8);
  or or_22 (or_22_out, not_26_out, not_27_out, C_4);
  xor xor_3 (xor_3_out, A_4, C_2);
  or or_23 (or_23_out, not_5_out, not_6_out);
  or or_24 (or_24_out, not_5_out, not_6_out);
  or or_25 (or_25_out, A_6, B_6);
  or or_26 (or_26_out, not_5_out, B_6);
  xor xor_4 (xor_4_out, A_3, C);
  or or_27 (or_27_out, and_3_out, and_4_out, and_5_out);
  // RGBLED rgbled_5: pin names not known; wires that end beside it: or_27_out
  or or_28 (or_28_out, and_6_out, and_7_out, and_8_out);
  // RGBLED rgbled_6: pin names not known; wires that end beside it: or_28_out
  and and_9 (and_9_out, or_1_out, or_2_out);
  and and_10 (and_10_out, or_3_out, or_4_out, or_5_out);
  // RGBLED rgbled_7: pin names not known; wires that end beside it: A_5, A_5, and_10_out
  xor xor_5 (xor_5_out, xor_3_out, B_4);
  // RGBLED rgbled_8: pin names not known; wires that end beside it: xor_5_out
  // RGBLED rgbled_9: pin names not known; wires that end beside it: and_9_out
  and and_11 (and_11_out, or_6_out, or_23_out);
  // RGBLED rgbled_10: pin names not known; wires that end beside it: and_11_out
  and and_12 (and_12_out, or_24_out, or_25_out, or_26_out);
  // RGBLED rgbled_11: pin names not known; wires that end beside it: and_12_out
  and and_13 (and_13_out, or_7_out, or_8_out, or_9_out, or_10_out);
  // RGBLED rgbled_12: pin names not known; wires that end beside it: and_13_out
  and and_14 (and_14_out, or_15_out, or_16_out, or_17_out, or_18_out);
  // RGBLED rgbled_13: pin names not known; wires that end beside it: and_14_out
  and and_15 (and_15_out, or_19_out, or_20_out, or_21_out, or_22_out);
  // RGBLED rgbled_14: pin names not known; wires that end beside it: and_15_out
  xor xor_6 (xor_6_out, xor_4_out, B_3);
  // RGBLED rgbled_15: pin names not known; wires that end beside it: xor_6_out
  and and_16 (and_16_out, or_11_out, or_12_out, or_13_out, or_14_out);
  // RGBLED rgbled_16: pin names not known; wires that end beside it: and_16_out

  // Notes on the sheet:
  //   Half Adder
  //   Half subtractor
  //   Full Adder
  //   Full subtractor
  //   HALF ADDER PRODUCT OF SUM
  //   HALF SUBTRACTOR PRODUCT OF SUM
  //   FULL ADDER PRODUCT FO SUMS
  //   FULL SUBTRACTOR PRODUCT OF SUMS
  //   SUM OF PRODUCTS
  //   SUM OF PRODUCTS
  //   SUM OF PRODUCTS
  //   SUM OF PRODUCTS
  //   SUM
  //   CARRY
  //   DIFFERENCE
  //   BORROW
  //   CARRY
  //   BORROW
  //   SUM
  //   CARRY
  //   DIFFERENCE
  //   DIFFERENCE
  //   BORROW
  //   SUM
  //   DIFFERENCE
  //   BORROW
  //   SUM
  //   CARRY
endmodule
