// Logisim project circuits.circ as structural Verilog: 1 circuit, main circuit main
module main (
  input  A,
  input  B,
  input  C,
  input  A_2,
  input  B_2,
  input  C_2,
  input  A_3,
  input  B_3,
  input  C_3,
  input  D,
  input  A_4,
  input  B_4,
  input  C_4,
  output out_14,
  output out_15,
  output out_16,
  output out_17
);

  wire and_1_out, and_2_out, and_3_out, and_4_out, and_5_out, and_6_out, and_7_out, and_8_out, and_9_out,
       and_10_out, and_11_out, and_12_out, and_13_out, not_1_out, not_2_out, not_3_out, not_4_out, not_5_out,
       not_6_out, not_7_out, not_8_out, not_9_out, not_10_out, or_1_out, or_2_out, or_3_out, or_4_out,
       or_5_out, or_6_out;

  not not_1 (not_1_out, B_2);
  not not_2 (not_2_out, C_2);
  not not_3 (not_3_out, B_3);
  or or_1 (or_1_out, A, B);
  or or_2 (or_2_out, B, C);
  not not_4 (not_4_out, B_2);
  or or_3 (or_3_out, not_1_out, C_2);
  or or_4 (or_4_out, B_2, not_2_out);
  not not_5 (not_5_out, C_4);
  not not_6 (not_6_out, C_4);
  not not_7 (not_7_out, not_4_out);
  and and_1 (and_1_out, A_3, not_3_out);
  and and_2 (and_2_out, B_3, D);
  not not_8 (not_8_out, A_4);
  not not_9 (not_9_out, B_4);
  and and_3 (and_3_out, A, B);
  and and_4 (and_4_out, or_1_out, or_2_out);
  and and_5 (and_5_out, A_2, or_3_out);
  and and_6 (and_6_out, not_7_out, or_4_out);
  not not_10 (not_10_out, B_3);
  and and_7 (and_7_out, A_4, B_4, C_4);
  and and_8 (and_8_out, not_8_out, not_9_out, not_5_out);
  and and_9 (and_9_out, not_8_out, B_4, C_4);
  and and_10 (and_10_out, A_4, not_9_out, C_4);
  and and_11 (and_11_out, A_4, not_9_out, not_6_out);
  and and_12 (and_12_out, A_2, not_4_out);
  or or_5 (or_5_out, and_2_out, C_3);
  or or_6 (or_6_out, A_3, not_10_out, C_3);
  and and_13 (and_13_out, and_1_out, or_5_out);
  or or_7 (out_14, and_3_out, and_4_out);
  or or_8 (out_15, and_12_out, and_5_out, and_6_out);
  or or_9 (out_16, and_13_out, or_6_out);
  or or_10 (out_17, and_7_out, and_8_out, and_9_out, and_10_out, and_11_out);

  // Notes on the sheet:
  //   1.
  //   2.
  //   3.
  //   4.
  //   AB+A(B+C)+B(B+C)
  //   AB’+A(B’+C)+B(B+C’)
  //   AB’(C+BD)+A’B’C
  //   A’BC+AB’C’+A’B’C’+AB’C+ABC
  //   CIRCUITS
  //   AB+A(B+C)+B(B+C)
  //   AB’+A(B’+C)+B(B+C’)
  //   AB’(C+BD)+A’B’C
  //   A’BC+AB’C’+A’B’C’+AB’C+ABC
endmodule
