// Logisim project DECODERS.circ as structural Verilog: 1 circuit, main circuit main
module main (
  input  in_1,
  input  in_2,
  input  in_3,
  input  in_4,
  input  in_5,
  input  in_6,
  input  B,
  input  EN,
  input  A,
  input  B_2,
  input  C,
  input  D
);

  wire and_1_out, and_2_out, and_3_out, and_4_out, and_5_out, and_6_out, and_7_out, and_8_out, and_9_out,
       and_10_out, and_11_out, and_12_out, and_13_out, and_14_out, and_15_out, and_16_out, and_17_out,
       and_18_out, and_19_out, and_20_out, and_21_out, and_22_out, and_23_out, and_24_out, and_25_out,
       and_26_out, and_27_out, and_28_out, not_1_out, not_2_out, not_3_out, not_4_out, not_5_out, not_6_out,
       not_7_out, not_8_out, not_9_out, not_10_out, not_11_out, not_12_out, not_14_out, not_15_out,
       not_16_out, not_17_out, not_18_out, not_19_out, not_20_out, not_21_out, not_22_out, not_23_out,
       not_24_out, not_25_out, not_26_out, not_27_out, not_28_out, not_29_out, not_30_out, not_31_out,
       not_32_out, not_33_out, not_34_out, not_35_out, not_36_out, not_37_out, not_38_out, not_39_out;

  not not_1 (not_1_out, in_2);
  not not_2 (not_2_out, in_6);
  not not_3 (not_3_out, B);
  not not_4 (not_4_out, in_6);
  not not_5 (not_5_out, B);
  not not_6 (not_6_out, in_3);
  and and_1 (and_1_out, in_5, not_2_out, not_3_out);
  LED led_1 (.in(and_1_out));
  and and_2 (and_2_out, in_5, not_4_out, B);
  LED led_2 (.in(and_2_out));
  and and_3 (and_3_out, in_5, in_6, not_5_out);
  LED led_3 (.in(and_3_out));
  and and_4 (and_4_out, in_5, in_6, B);
  LED led_4 (.in(and_4_out));
  not not_7 (not_7_out, in_4);
  not not_8 (not_8_out, B_2);
  not not_9 (not_9_out, D);
  not not_10 (not_10_out, B_2);
  not not_11 (not_11_out, B_2);
  not not_12 (not_12_out, D);
  // NOT_Gate not_13 has open pins: in=A, out=open
  not not_14 (not_14_out, B_2);
  not not_15 (not_15_out, A);
  not not_16 (not_16_out, D);
  not not_17 (not_17_out, A);
  not not_18 (not_18_out, A);
  not not_19 (not_19_out, D);
  not not_20 (not_20_out, A);
  not not_21 (not_21_out, D);
  not not_22 (not_22_out, D);
  not not_23 (not_23_out, D);
  not not_24 (not_24_out, D);
  and and_5 (and_5_out, in_1, not_1_out, not_6_out, not_7_out);
  LED led_5 (.in(and_5_out));
  and and_6 (and_6_out, in_1, not_1_out, not_6_out, in_4);
  LED led_6 (.in(and_6_out));
  and and_7 (and_7_out, in_1, not_1_out, in_3, not_7_out);
  LED led_7 (.in(and_7_out));
  and and_8 (and_8_out, in_1, not_1_out, in_3, in_4);
  LED led_8 (.in(and_8_out));
  and and_9 (and_9_out, in_1, in_2, not_6_out, not_7_out);
  LED led_9 (.in(and_9_out));
  and and_10 (and_10_out, in_1, in_2, not_6_out, in_4);
  LED led_10 (.in(and_10_out));
  and and_11 (and_11_out, in_1, in_2, in_3, not_7_out);
  LED led_11 (.in(and_11_out));
  and and_12 (and_12_out, in_1, in_2, in_3, in_4);
  LED led_12 (.in(and_12_out));
  not not_25 (not_25_out, A);
  and and_13 (and_13_out, EN, not_25_out, not_8_out, not_26_out, not_9_out);
  LED led_13 (.in(and_13_out));
  not not_26 (not_26_out, C);
  not not_27 (not_27_out, A);
  and and_14 (and_14_out, EN, not_27_out, not_10_out, not_28_out, D);
  LED led_14 (.in(and_14_out));
  not not_28 (not_28_out, C);
  not not_29 (not_29_out, A);
  and and_15 (and_15_out, EN, not_29_out, not_11_out, C, not_12_out);
  LED led_15 (.in(and_15_out));
  and and_16 (and_16_out, EN, EN, not_14_out, C, D);
  LED led_16 (.in(and_16_out));
  and and_17 (and_17_out, EN, not_15_out, B_2, not_30_out, not_16_out);
  LED led_17 (.in(and_17_out));
  not not_30 (not_30_out, C);
  and and_18 (and_18_out, EN, not_17_out, B_2, not_31_out, D);
  LED led_18 (.in(and_18_out));
  not not_31 (not_31_out, C);
  and and_19 (and_19_out, EN, not_18_out, B_2, C, not_19_out);
  LED led_19 (.in(and_19_out));
  and and_20 (and_20_out, EN, not_20_out, B_2, C, D);
  LED led_20 (.in(and_20_out));
  not not_32 (not_32_out, B_2);
  and and_21 (and_21_out, EN, A, not_32_out, not_33_out, not_21_out);
  LED led_21 (.in(and_21_out));
  not not_33 (not_33_out, C);
  not not_34 (not_34_out, B_2);
  and and_22 (and_22_out, EN, A, not_34_out, not_35_out, D);
  LED led_22 (.in(and_22_out));
  not not_35 (not_35_out, C);
  not not_36 (not_36_out, B_2);
  and and_23 (and_23_out, EN, A, not_36_out, C, not_22_out);
  LED led_23 (.in(and_23_out));
  not not_37 (not_37_out, B_2);
  and and_24 (and_24_out, EN, A, not_37_out, C, D);
  LED led_24 (.in(and_24_out));
  and and_25 (and_25_out, EN, A, B_2, not_38_out, not_23_out);
  LED led_25 (.in(and_25_out));
  not not_38 (not_38_out, C);
  and and_26 (and_26_out, EN, A, B_2, not_39_out, D);
  LED led_26 (.in(and_26_out));
  not not_39 (not_39_out, C);
  and and_27 (and_27_out, EN, A, B_2, C, not_24_out);
  LED led_27 (.in(and_27_out));
  and and_28 (and_28_out, EN, A, B_2, C, D);
  LED led_28 (.in(and_28_out));

  // Notes on the sheet:
  //   3 INPUT DECODER
  //   EN
  //   2 INPUT DECODER
  //   A
  //   EN
  //   4 INPUT DECODER
  //   A
  //   B
  //   C
  //   y0
  //   y1
  //   y2
  //   y3
  //   yo
  //   y1
  //   y2
  //   y3
  //   y4
  //   y5
  //   y6
  //   y7
  //   y0
  //   y1
  //   y2
  //   y3
  //   y4
  //   y5
  //   y6
  //   y7
  //   y8
  //   y9
  //   y10
  //   y11
  //   y12
  //   y13
  //   y14
  //   y15
endmodule
