// Logisim project ENCODERS.circ as structural Verilog: 1 circuit, main circuit main
module main (
  input  Y3,
  input  Y2,
  input  Y1,
  input  _3,
  input  _2,
  input  _1,
  input  _1_2,
  input  _2_2,
  input  _3_2,
  input  _4,
  input  _5,
  input  _6,
  input  _7,
  input  in_14,
  input  in_15,
  input  in_16,
  input  in_17,
  input  in_18,
  input  _6_2,
  input  in_20,
  input  in_21,
  input  in_22,
  input  in_23,
  input  _11,
  input  in_25,
  input  in_26,
  input  in_27,
  input  in_28
);

  wire and_1_out, not_1_out, or_1_out, or_2_out, or_3_out, or_4_out, or_5_out, or_6_out, or_7_out, or_8_out,
       or_9_out, or_10_out, or_11_out;

  not not_1 (not_1_out, _2);
  and and_1 (and_1_out, not_1_out, _1);
  or or_1 (or_1_out, Y3, Y2);
  LED led_1 (.in(or_1_out));
  or or_2 (or_2_out, Y3, Y1);
  LED led_2 (.in(or_2_out));
  or or_3 (or_3_out, _3, _2);
  LED led_3 (.in(or_3_out));
  or or_4 (or_4_out, and_1_out, _3);
  LED led_4 (.in(or_4_out));
  or or_5 (or_5_out, _7, _6, _5, _4);
  LED led_5 (.in(or_5_out));
  or or_6 (or_6_out, _7, _6, _3_2, _2_2);
  LED led_6 (.in(or_6_out));
  or or_7 (or_7_out, _7, _5, _3_2, _1_2);
  LED led_7 (.in(or_7_out));
  or or_8 (or_8_out, in_28, in_27, in_26, in_25, _11, in_23, in_22, in_21);
  LED led_8 (.in(or_8_out));
  or or_9 (or_9_out, in_17, in_18, _6_2, in_20, in_28, in_27, in_26, in_25);
  LED led_9 (.in(or_9_out));
  or or_10 (or_10_out, in_15, in_16, _6_2, in_20, in_23, _11, in_27, in_28);
  LED led_10 (.in(or_10_out));
  or or_11 (or_11_out, in_14, in_16, in_18, in_20, in_22, _11, in_26, in_28);
  LED led_11 (.in(or_11_out));

  // Notes on the sheet:
  //   4-2 ENCODER
  //   4-2 PRIORITY ENCODER
  //   8-3 ENCODER
  //   16 - 4 ENCODER
  //   2
  //   1
  //   3
  //   4
  //   5
  //   7
  //   9
  //   8
  //   10
  //   12
  //   13
  //   14
  //   15
  //   3
  //   2
  //   1
  //   0
endmodule
